# Fritzing sketch MyProject (saved by Fritzing 0.9.4)
breadboards: 1

parts:
  Parça1 = Arduino Uno (Rev3)
  U1 = NodeMCU V3.0
  T1 = LM35 Temperature Sensor [package="TO92 [THT]"]
  R1 = Photocell (LDR) [package=THT]
  R2 = Resistor [tolerance=±5% resistance=220 package=THT]
  J2 = Basic Servo

nets:
  N1: Parça1.A1, R1.pin_1, R2.Pin_0
  N2: Parça1.D9_PWM, J2.pulse
  N3: Parça1.ioref, T1.+Vs
  5V: Parça1.5V, R1.pin_0, J2.vcc
  GND: Parça1.GND, T1.GND, R2.Pin_1, J2.gnd
  N4: U1.GND#16, U1.GND#33
  N5: U1.A0, T1.Vout

custom parts:
  NodeMCU V3.0: ESP8266 based NodeMCU
